// Logisim project Simulacion_proyecto01.circ as structural Verilog: 1 circuit, main circuit main
module main (
);

  wire dipswitch_1_p1, dipswitch_2_p1, n7404_1_pin4, n7404_1_pin6, n7408_1_pin3, n7408_1_pin6, n7432_1_pin3;

  // DipSwitch #(.number(1)) dipswitch_1: pin names not known; wires that end beside it: dipswitch_1_p1
  // DipSwitch #(.number(1)) dipswitch_2: pin names not known; wires that end beside it: dipswitch_2_p1
  _7404 u_7404_1 (
    .pin3(dipswitch_1_p1), .pin4(n7404_1_pin4), .pin5(dipswitch_2_p1), .pin6(n7404_1_pin6));  // open: pin1, pin2, pin13, pin12, pin11, pin10, pin9, pin8
  _7408 u_7408_1 (
    .pin1(n7404_1_pin6), .pin2(n7404_1_pin4), .pin3(n7408_1_pin3), .pin4(dipswitch_2_p1),
    .pin5(dipswitch_1_p1), .pin6(n7408_1_pin6));  // open: pin13, pin12, pin11, pin10, pin9, pin8
  _7432 u_7432_1 (
    .pin1(n7408_1_pin6), .pin2(n7408_1_pin3), .pin3(n7432_1_pin3));  // open: pin4, pin5, pin6, pin13, pin12, pin11, pin10, pin9, pin8
  LED led_1 (.in(n7432_1_pin3));

  // Notes on the sheet:
  //   A
  //   B
endmodule
