// Logisim project Circuito_logico_Proyecto02.circ as structural Verilog: 1 circuit, main circuit main
module main (
);

  wire and_1_out, and_2_out, and_3_out, and_4_out, and_5_out, not_1_out, not_2_out, not_3_out, not_4_out,
       undriven, undriven_2, undriven_3, undriven_4, undriven_5, undriven_6;

  not not_1 (not_1_out, undriven);
  not not_2 (not_2_out, undriven_2);
  and and_1 (and_1_out, not_1_out, undriven_2);
  and and_2 (and_2_out, not_1_out, undriven_3);
  LED led_1 (.in(undriven));
  LED led_2 (.in(and_1_out));
  LED led_3 (.in(and_2_out));
  not not_3 (not_3_out, undriven_6);
  not not_4 (not_4_out, undriven_4);
  and and_3 (and_3_out, not_3_out, undriven_4);
  LED led_4 (.in(undriven_6));
  LED led_5 (.in(and_3_out));
  buf and_4 (and_4_out, undriven_5);  // AND_Gate
  and and_5 (and_5_out, not_3_out, and_4_out);
  LED led_6 (.in(and_5_out));

  // Notes on the sheet:
  //   A
  //   B
  //   C
  //   A
  //   B
  //   C
endmodule
