// Logisim project Simulacion_proyecto_2.circ as structural Verilog: 1 circuit, main circuit main
module main (
);

  wire dipswitch_1_sw1, dipswitch_1_sw2, dipswitch_1_sw3, n7404_1_pin4, n7404_1_pin6, n7408_1_pin3,
       n7408_1_pin6, n7408_1_pin11;

  DipSwitch #(.number(4)) dipswitch_1 (
    .sw1(dipswitch_1_sw1), .sw2(dipswitch_1_sw2), .sw3(dipswitch_1_sw3));  // open: sw4
  _7404 u_7404_1 (
    .pin3(dipswitch_1_sw2), .pin4(n7404_1_pin4), .pin5(dipswitch_1_sw3), .pin6(n7404_1_pin6));  // open: pin1, pin2, pin13, pin12, pin11, pin10, pin9, pin8
  _7408 u_7408_1 (
    .pin1(dipswitch_1_sw1), .pin2(n7404_1_pin4), .pin3(n7408_1_pin3), .pin4(n7408_1_pin3),
    .pin5(n7404_1_pin6), .pin6(n7408_1_pin6), .pin13(dipswitch_1_sw2), .pin12(n7404_1_pin6),
    .pin11(n7408_1_pin11));  // open: pin10, pin9, pin8
  LED led_1 (.in(n7408_1_pin11));
  LED led_2 (.in(dipswitch_1_sw3));
  LED led_3 (.in(n7408_1_pin6));
endmodule
